// Digital circuit mode_selector.dig as structural Verilog
module mode_selector (
  input  ID,
  input  PWD,
  input  DIS,
  input  RESET,
  input  CLK,
  input  RST,
  output IDO,
  output PWDO
);

  wire and_1_out, and_2_out, not_1_out, not_2_out, not_3_out, not_4_out, or_1_out;

  not not_1 (not_1_out, RST);
  not not_2 (not_2_out, DIS);
  or or_1 (or_1_out, not_1_out, RESET);
  and and_1 (and_1_out, not_2_out, PWD);
  not not_3 (not_3_out, PWD);
  and and_2 (and_2_out, not_3_out, not_4_out, ID);
  not not_4 (not_4_out, DIS);
  JK_FF_AS jk_ff_as_1 (.Set(1'b0), .J(and_1_out), .C(CLK), .K(and_2_out), .Clr(or_1_out), .Q(PWDO), .nQ(IDO));
endmodule
