// Digital circuit proj_reg.dig as structural Verilog
module proj_reg (
  input  [3:0] D,
  input  C,
  input  CLR,
  input  EN,
  output [3:0] Q
);

  wire [3:0] multiplexer_1_out;

  Multiplexer #(.Bits(4)) multiplexer_1 (.sel(EN), .in_0(Q), .in_1(D), .out(multiplexer_1_out));
  D_FF_AS d_ff_as_1 (.Set(1'b0), .D(multiplexer_1_out[0]), .C(C), .Clr(CLR), .Q(Q[0]));  // open: nQ
  D_FF_AS d_ff_as_2 (.Set(1'b0), .D(multiplexer_1_out[1]), .C(C), .Clr(CLR), .Q(Q[1]));  // open: nQ
  D_FF_AS d_ff_as_3 (.Set(1'b0), .D(multiplexer_1_out[2]), .C(C), .Clr(CLR), .Q(Q[2]));  // open: nQ
  D_FF_AS d_ff_as_4 (.Set(1'b0), .D(multiplexer_1_out[3]), .C(C), .Clr(CLR), .Q(Q[3]));  // open: nQ
  // Pins of 1 and 4 bits meet at Q
endmodule
