// Digital circuit shifter.dig as structural Verilog
module shifter (
  input  [3:0] IN,
  input  EN,
  input  DA,
  input  CLK,
  input  RST,
  output [3:0] ID1,
  output [3:0] ID0,
  output [6:0] HEX
);

  wire and_1_out, not_1_out;
  wire [13:0] mul_1_mul;

  not not_1 (not_1_out, RST);
  and and_1 (and_1_out, DA, EN);
  // proj_reg proj_reg_1: pin names not known; wires that end beside it: IN, CLK, not_1_out, and_1_out, ID0, ID1, ID0
  // proj_reg proj_reg_2: pin names not known; wires that end beside it: ID0, CLK, not_1_out, and_1_out, ID1
  Mul #(.Bits(7)) mul_1 (.a({3'b000, ID1}), .b(7'b0001010), .mul(mul_1_mul));
  Add #(.Bits(7)) add_1 (.a(mul_1_mul[6:0]), .b({3'b000, ID0}), .c_i(1'b0), .s(HEX));  // open: c_o
endmodule
