// Digital circuit shifter_pwd.dig as structural Verilog
module shifter_pwd (
  input  [3:0] DATA_in,
  input  [15:0] PWD_in,
  input  DA,
  input  EN,
  input  RST,
  input  CLK,
  output MATCH,
  output LED1,
  output LED2,
  output LED3,
  output LED4
);

  wire and_1_out, and_2_out, and_3_out, nand_1_out;
  wire [3:0] proj_reg_1_p5, proj_reg_2_p5, proj_reg_3_p5, proj_reg_4_p5;

  nand nand_1 (nand_1_out, EN, RST);
  // proj_reg proj_reg_1: pin names not known; wires that end beside it: DATA_in, CLK, nand_1_out, DA, proj_reg_1_p5
  // proj_reg proj_reg_2: pin names not known; wires that end beside it: proj_reg_1_p5, CLK, nand_1_out, DA, proj_reg_2_p5
  and and_1 (and_1_out, LED1, DA);
  and and_2 (and_2_out, LED2, and_1_out);
  and and_3 (and_3_out, LED3, and_2_out);
  // proj_reg proj_reg_3: pin names not known; wires that end beside it: proj_reg_2_p5, CLK, nand_1_out, DA, proj_reg_3_p5
  JK_FF_AS jk_ff_as_1 (.Set(1'b0), .J(DA), .C(CLK), .K(1'b0), .Clr(nand_1_out), .Q(LED1));  // open: nQ
  JK_FF_AS jk_ff_as_2 (.Set(1'b0), .J(and_1_out), .C(CLK), .K(1'b0), .Clr(nand_1_out), .Q(LED2));  // open: nQ
  JK_FF_AS jk_ff_as_3 (.Set(1'b0), .J(and_2_out), .C(CLK), .K(1'b0), .Clr(nand_1_out), .Q(LED3));  // open: nQ
  JK_FF_AS jk_ff_as_4 (.Set(1'b0), .J(and_3_out), .C(CLK), .K(1'b0), .Clr(nand_1_out), .Q(LED4));  // open: nQ
  // proj_reg proj_reg_4: pin names not known; wires that end beside it: proj_reg_3_p5, CLK, nand_1_out, DA, proj_reg_4_p5
  Comparator #(.Bits(16)) comparator_1 (
    .a(PWD_in), .b({proj_reg_4_p5, proj_reg_3_p5, proj_reg_2_p5, proj_reg_1_p5}), .eq(MATCH));  // open: gt, lt
endmodule
