// Digital circuit timer.dig as structural Verilog
module timer (
  input  START,
  input  CLK,
  input  RST,
  output RESET,
  output DIS
);

  wire and_1_out, and_2_out, and_3_out, and_4_out, and_5_out, and_6_out, and_7_out, and_8_out, or_1_out;
  wire [8:0] jk_ff_as_9_q;

  or or_1 (or_1_out, RESET, ~RST);  // Or
  and and_1 (and_1_out, jk_ff_as_9_q[0], START);
  and and_2 (and_2_out, jk_ff_as_9_q[1], and_1_out);
  and and_3 (and_3_out, jk_ff_as_9_q[2], and_2_out);
  and and_4 (and_4_out, jk_ff_as_9_q[3], and_3_out);
  and and_5 (and_5_out, jk_ff_as_9_q[4], and_4_out);
  and and_6 (and_6_out, jk_ff_as_9_q[5], and_5_out);
  and and_7 (and_7_out, jk_ff_as_9_q[6], and_6_out);
  and and_8 (and_8_out, jk_ff_as_9_q[7], and_7_out);
  JK_FF_AS jk_ff_as_1 (.Set(1'b0), .J(START), .C(CLK), .K(START), .Clr(or_1_out), .Q(jk_ff_as_9_q[0]));  // open: nQ
  JK_FF_AS jk_ff_as_2 (
    .Set(1'b0), .J(and_1_out), .C(CLK), .K(and_1_out), .Clr(or_1_out), .Q(jk_ff_as_9_q[1]));  // open: nQ
  JK_FF_AS jk_ff_as_3 (
    .Set(1'b0), .J(and_2_out), .C(CLK), .K(and_2_out), .Clr(or_1_out), .Q(jk_ff_as_9_q[2]));  // open: nQ
  JK_FF_AS jk_ff_as_4 (
    .Set(1'b0), .J(and_3_out), .C(CLK), .K(and_3_out), .Clr(or_1_out), .Q(jk_ff_as_9_q[3]));  // open: nQ
  JK_FF_AS jk_ff_as_5 (
    .Set(1'b0), .J(and_4_out), .C(CLK), .K(and_4_out), .Clr(or_1_out), .Q(jk_ff_as_9_q[4]));  // open: nQ
  JK_FF_AS jk_ff_as_6 (
    .Set(1'b0), .J(and_5_out), .C(CLK), .K(and_5_out), .Clr(or_1_out), .Q(jk_ff_as_9_q[5]));  // open: nQ
  JK_FF_AS jk_ff_as_7 (
    .Set(1'b0), .J(and_6_out), .C(CLK), .K(and_6_out), .Clr(or_1_out), .Q(jk_ff_as_9_q[6]));  // open: nQ
  JK_FF_AS jk_ff_as_8 (
    .Set(1'b0), .J(and_7_out), .C(CLK), .K(and_7_out), .Clr(or_1_out), .Q(jk_ff_as_9_q[7]));  // open: nQ
  JK_FF_AS jk_ff_as_9 (
    .Set(1'b0), .J(and_8_out), .C(CLK), .K(and_8_out), .Clr(or_1_out), .Q(jk_ff_as_9_q[8]));  // open: nQ
  Comparator #(.Bits(9)) comparator_1 (.a(jk_ff_as_9_q), .b(9'h12c), .eq(RESET));  // open: gt, lt

  assign DIS = START;
endmodule
